// Logisim project HW3-403105939.circ as structural Verilog: 4 circuits, main circuit main
module main (
  input  Divide,
  input  Clk,
  input  Start,
  input  Rst,
  input  [31:0] A,
  input  [31:0] B,
  output [31:0] Result_Lo,
  output [31:0] Result_Hi,
  output Done
);

  wire c_u_1_write_e;
  wire [63:0] div_1_result, mul_1_result;

  MUL mul_1 (.A(A), .Start(Start), .Write_E(c_u_1_write_e), .Clk(Clk), .B(B), .Rst(Rst), .Result(mul_1_result));
  Multiplexer #(.width(64)) multiplexer_1 (
    .in0(mul_1_result), .in1(div_1_result), .out({Result_Hi, Result_Lo}), .sel(Divide));
  C_U c_u_1 (.Rst(Rst), .Clk(Clk), .Done(Done), .Write_E(c_u_1_write_e));  // open: Start
  DIV div_1 (.Write_E(c_u_1_write_e), .Clk(Clk), .B(B), .A(A), .Rst(Rst), .Start(Start), .Result(div_1_result));
endmodule

module MUL (
  input  [31:0] A,
  input  Start,
  input  Write_E,
  input  Clk,
  input  [31:0] B,
  input  Rst,
  output [63:0] Result
);

  wire and_1_out;
  wire [31:0] adder_1_out;
  wire [32:0] multiplexer_1_out;
  wire [32:32] adder_1_cout;
  wire [63:0] multiplexer_2_out;

  and and_1 (and_1_out, Write_E, Clk);
  Register #(.width(64)) register_1 (.D(multiplexer_2_out), .en(Write_E), .clk(and_1_out), .Q(Result), .clr(Rst));
  Adder #(.width(32)) adder_1 (.a(A), .b(Result[63:32]), .out(adder_1_out), .cout(adder_1_cout[32]));  // open: cin
  Multiplexer #(.width(33)) multiplexer_1 (
    .in0({1'b0, Result[63:32]}), .in1({adder_1_cout[32], adder_1_out}), .out(multiplexer_1_out),
    .sel(Result[0]));
  Multiplexer #(.width(64)) multiplexer_2 (
    .in0({multiplexer_1_out, Result[31:1]}), .in1({{32{1'b0}}, B}), .out(multiplexer_2_out), .sel(Start));
endmodule

module DIV (
  input  Write_E,
  input  Clk,
  input  [31:0] B,
  input  [31:0] A,
  input  Rst,
  input  Start,
  output [63:0] Result
);

  wire and_1_out, not_2_out;
  wire [0:0] adder_1_cout;
  wire [31:0] adder_1_out, multiplexer_1_out, not_1_out;
  wire [63:0] multiplexer_2_out;

  Register #(.width(64)) register_1 (.D(multiplexer_2_out), .en(Write_E), .clk(and_1_out), .Q(Result), .clr(Rst));
  and and_1 (and_1_out, Write_E, Clk);
  assign not_1_out = ~B;  // NOT_Gate not_1, 32 bits wide
  Adder #(.width(32)) adder_1 (.a(Result[62:31]), .b(not_1_out), .out(adder_1_out), .cin(1'b1), .cout(adder_1_cout[0]));
  not not_2 (not_2_out, adder_1_cout[0]);
  Multiplexer #(.width(32)) multiplexer_1 (
    .in0(adder_1_out), .in1(Result[62:31]), .out(multiplexer_1_out), .sel(not_2_out));
  Multiplexer #(.width(64)) multiplexer_2 (
    .in0({multiplexer_1_out, Result[30:0], adder_1_cout[0]}), .in1({{32{1'b0}}, A}), .out(multiplexer_2_out),
    .sel(Start));
endmodule

module C_U (
  input  Start,
  input  Rst,
  input  Clk,
  output Done,
  output Write_E
);

  wire or_1_out, or_2_out;
  wire [5:0] adder_1_out, multiplexer_1_out, register_1_q;

  Register #(.width(6)) register_1 (.D(multiplexer_1_out), .en(or_2_out), .clk(Clk), .Q(register_1_q), .clr(Rst));
  Comparator #(.width(6)) comparator_1 (.a(register_1_q), .b(6'b100001), .eq(Done));  // open: gt, lt
  or or_1 (or_1_out, Start, Rst);
  Adder #(.width(6)) adder_1 (.a(register_1_q), .b(6'b000001), .out(adder_1_out));  // open: cin, cout
  not not_1 (Write_E, Done);
  Multiplexer #(.width(6)) multiplexer_1 (.in0(adder_1_out), .in1(6'b000001), .out(multiplexer_1_out), .sel(or_1_out));
  or or_2 (or_2_out, or_1_out, Write_E);
endmodule
